// Digital circuit ALU.dig as structural Verilog
module ALU (
  input  [15:0] A,
  input  [15:0] B,
  input  [3:0] Op,
  input  Ci,
  output [15:0] Y,
  output O,
  output Z,
  output N
);

  wire add_1_c_o, sub_1_c_o;
  wire [15:0] add_1_s, and_1_out, mul_1_mul, neg_1_out, or_1_out, sub_1_s, xor_1_out;
  wire [31:16] mul_1_mul_2;

  Add #(.Bits(16)) add_1 (.a(A), .b(B), .c_i(Ci), .s(add_1_s), .c_o(add_1_c_o));
  Sub #(.Bits(16)) sub_1 (.a(A), .b(B), .c_i(Ci), .s(sub_1_s), .c_o(sub_1_c_o));
  Mul #(.Bits(16)) mul_1 (.a(A), .b(B), .mul({mul_1_mul_2, mul_1_mul}));
  assign and_1_out = A & B;  // And and_1, 16 bits wide
  assign or_1_out = A | B;  // Or or_1, 16 bits wide
  assign xor_1_out = A ^ B;  // XOr xor_1, 16 bits wide
  Neg #(.Bits(16)) neg_1 (.in(A), .out(neg_1_out));
  Multiplexer #(.Selector_Bits(4), .Bits(16)) multiplexer_1 (
    .sel(Op), .in_0(add_1_s), .in_1(sub_1_s), .in_2(mul_1_mul), .in_3(and_1_out), .in_4(or_1_out),
    .in_5(xor_1_out), .in_6(neg_1_out), .in_7({16{1'b0}}), .in_8({16{1'b0}}), .in_9({16{1'b0}}),
    .in_10({16{1'b0}}), .in_11({16{1'b0}}), .in_12({16{1'b0}}), .in_13({16{1'b0}}), .in_14({16{1'b0}}),
    .in_15({16{1'b0}}), .out({N, Y[14:0]}));
  Multiplexer #(.Selector_Bits(4)) multiplexer_2 (
    .sel(Op), .in_0(add_1_c_o), .in_1(sub_1_c_o), .in_2(1'b0), .in_3(1'b0), .in_4(1'b0), .in_5(1'b0),
    .in_6(1'b0), .in_7(1'b0), .in_8(1'b0), .in_9(1'b0), .in_10(1'b0), .in_11(1'b0), .in_12(1'b0),
    .in_13(1'b0), .in_14(1'b0), .in_15(1'b0), .out(O));
  Comparator #(.Bits(16)) comparator_1 (.a({N, Y[14:0]}), .b({16{1'b0}}), .eq(Z));  // open: gt, lt

  assign Y[15] = N;

  // Other names for the same wires on the sheet: sel[3:0] = Op

  // Notes on the sheet:
  //   A: Number 1
  //   B: Number 2
  //   Y: Result of operation
  //   Op: Select number, what ALU op to do.
  //   O: Carry out, can also act as an overflow flag.
  //   Ci: Carry in
  //   Z: High if the result number is zero.
  //   N: High if the resultant number is negative
endmodule
