// Digital circuit computer.dig as structural Verilog
module computer (
  input  clk,
  input  Clock_Enable,
  input  [15:0] Data_Bus_Manual_Input,
  input  Manual_Clock_Tick,
  input  Data_bus_manual_override
);

  wire ALUn, ALUo, ALUz, Clock, DBout, driverinvsel_1_out, driverinvsel_4_out, HLT, IRwr, MARwr, not_1_out,
       or_1_out, OUTwr, PCin, PCwr, RAMre, RAMwr, RAre, RAwr, RBre, RBwr, ROMre, SCclr, SUMre, SUMwr;
  wire [2:0] alu_1_o, counter_1_out;
  wire [3:0] ALUop, Output_Register_q, Output_Register_q_2, Output_Register_q_3, Output_Register_q_4;
  wire [4:0] bitcount_1_out;
  wire [5:0] Instruction_Register_q;
  wire [9:0] add_1_s, driverinvsel_3_out, Instruction_Register_q_2, Memory_Address_Register_q,
       Program_Counter_q;
  wire [15:0] alu_1_y, databus, Register_A_q, Register_B_q, Sum_Register_q;
  wire [20:0] Con__Logic_Table_d, Logic_Table_d;

  assign driverinvsel_1_out = ~HLT ? clk : 1'bz;  // DriverInvSel driverinvsel_1
  Seven_Seg_Hex seven_seg_hex_1 (.d(Output_Register_q_4), .dp(1'b0));
  assign Clock = ~Clock_Enable ? Manual_Clock_Tick : 1'bz;  // DriverInvSel driverinvsel_2
  assign Clock = Clock_Enable ? driverinvsel_1_out : 1'bz;  // Driver driver_1
  Seven_Seg_Hex seven_seg_hex_2 (.d(Output_Register_q_3), .dp(1'b0));
  LED led_1 (.in(Clock_Enable));
  assign driverinvsel_3_out = ~PCin ? databus[9:0] : 10'bz;  // DriverInvSel driverinvsel_3
  assign driverinvsel_3_out = PCin ? add_1_s : 10'bz;  // Driver driver_2
  Seven_Seg_Hex seven_seg_hex_3 (.d(Output_Register_q_2), .dp(1'b0));
  Register #(.Bits(10)) Memory_Address_Register (
    .D(databus[9:0]), .C(Clock), .en(MARwr), .Q(Memory_Address_Register_q));
  Register #(.Bits(10), .isProgramCounter("true")) Program_Counter (
    .D(driverinvsel_3_out), .C(Clock), .en(driverinvsel_4_out), .Q(Program_Counter_q));
  assign driverinvsel_4_out = ~PCin ? PCwr : 1'bz;  // DriverInvSel driverinvsel_4
  assign driverinvsel_4_out = PCin ? 1'b1 : 1'bz;  // Driver driver_3
  Add #(.Bits(10)) add_1 (.a(10'h1), .b(Program_Counter_q), .c_i(1'b0), .s(add_1_s));  // open: c_o
  Seven_Seg_Hex seven_seg_hex_4 (.d(Output_Register_q), .dp(1'b0));
  RAMDualPort #(.AddrBits(10), .Bits(16)) RAM (
    .A(Memory_Address_Register_q), .Din(databus), .str(RAMwr), .C(Clock), .ld(RAMre), .D(databus));
  ROM #(.AddrBits(10), .isProgramMemory("true"), .Bits(16)) Program (.A(Program_Counter_q), .sel(ROMre), .D(databus));
  Register #(.Bits(16)) Output_Register (
    .D(databus), .C(Clock), .en(OUTwr),
    .Q({Output_Register_q_4, Output_Register_q_3, Output_Register_q_2, Output_Register_q}));
  assign databus = Data_bus_manual_override ? Data_Bus_Manual_Input : 16'bz;  // Driver driver_4
  assign databus = RAre ? Register_A_q : 16'bz;  // Driver driver_5
  assign databus = SUMre ? Sum_Register_q : 16'bz;  // Driver driver_6
  assign databus = RBre ? Register_B_q : 16'bz;  // Driver driver_7
  Register #(.Bits(16)) Instruction_Register (
    .D(databus), .C(Clock), .en(IRwr), .Q({Instruction_Register_q_2, Instruction_Register_q}));
  assign databus = DBout ? {{6{1'b0}}, Instruction_Register_q_2} : 16'bz;  // Driver driver_8
  Register #(.Bits(16)) Register_A (.D(databus), .C(Clock), .en(RAwr), .Q(Register_A_q));
  Register #(.Bits(16)) Register_B (.D(databus), .C(Clock), .en(RBwr), .Q(Register_B_q));
  not not_1 (not_1_out, Clock);
  Counter #(.Bits(3)) counter_1 (.en(1'b1), .C(not_1_out), .clr(SCclr), .out(counter_1_out));  // open: ovf
  Register #(.Bits(16)) Sum_Register (.D(alu_1_y), .C(Clock), .en(SUMwr), .Q(Sum_Register_q));
  ALU alu_1 (
    .A(Register_A_q), .B(Register_B_q), .Op(ALUop), .Ci(1'b0), .Y(alu_1_y), .O(alu_1_o[0]), .Z(alu_1_o[1]),
    .N(alu_1_o[2]));
  ROM #(.AddrBits(9), .Bits(21)) Logic_Table (
    .A({Instruction_Register_q, counter_1_out}), .sel(1'b1), .D(Logic_Table_d));
  BitCount #(.Bits(21)) bitcount_1 (.in(Con__Logic_Table_d), .out(bitcount_1_out));
  ROM #(.AddrBits(11), .Bits(21)) Con__Logic_Table (
    .A({Instruction_Register_q, ALUo, ALUz, counter_1_out}), .sel(1'b1), .D(Con__Logic_Table_d));
  or or_1 (or_1_out, bitcount_1_out[0], bitcount_1_out[1], bitcount_1_out[2], bitcount_1_out[3], bitcount_1_out[4]);
  assign {OUTwr, HLT, DBout, ALUop, SUMwr, SUMre, RAre, RAwr, RBre, RBwr, RAMwr, RAMre, MARwr, PCwr, PCin, ROMre, IRwr, SCclr} = ~or_1_out ? Logic_Table_d : 21'bz;  // DriverInvSel driverinvsel_5
  assign {OUTwr, HLT, DBout, ALUop, SUMwr, SUMre, RAre, RAwr, RBre, RBwr, RAMwr, RAMre, MARwr, PCwr, PCin, ROMre, IRwr, SCclr} = or_1_out ? Con__Logic_Table_d : 21'bz;  // Driver driver_9
  Register #(.Bits(3)) ALU_Flag_Register (.D(alu_1_o), .C(Clock), .en(SUMwr), .Q({ALUn, ALUz, ALUo}));

  // Notes on the sheet:
  //   clk: Hz: 50
  //   contents of Program (hex, n*v repeats v):
  //   b,0,1,8,18e,cc,3,c,d,7
  //   contents of Logic_Table (hex, n*v repeats v):
  //   e,1,6*0,e,40020,441,5*0,e,40020,881,5*0,e,40d,6*0,e,40020,141
  //   ,5*0,e,40020,281,5*0,e,10d,6*0,e,8ac7230489e80001,6*0,e,40020
  //   ,140,2000,1401,0,0,0,e,40020,140,6000,1401,0,0,0,e,40020,140,a000
  //   ,1401,0,0,0,e,40020,8d,5*0,e,40011,6*0,e,100801,6*0,e
  //   contents of Con__Logic_Table (hex, n*v repeats v):
  //   457*0,40011
endmodule
